// Logisim project FPA_Circuit.circ as structural Verilog: 9 circuits, main circuit Normalizing Hardware
// Normalizing \nHardware
module Normalizing_Hardware (
  input  [3:0] Exponent,
  input  [15:0] Significand,
  output Not_All_Zero,
  output [15:0] Significand_Output,
  output [3:0] Exponent_Output
);

  wire and_1_out, and_2_out, and_3_out, nor_1_out, or_1_out, subtractor_1_bout, xor_1_out;
  wire [3:0] multiplexer_1_out, multiplexer_3_out, set_bit_finder_1_shift_amount, subtractor_1_out,
       subtractor_2_out;
  wire [15:0] shifter_1_out;

  and and_1 (and_1_out, Exponent[3], Exponent[2], Exponent[1], Exponent[0]);
  Subtractor #(.width(4)) subtractor_1 (
    .a(Exponent), .b(set_bit_finder_1_shift_amount), .out(subtractor_1_out), .bin(1'b0),
    .bout(subtractor_1_bout));
  Multiplexer #(.width(4), .disabled(0), .enable("false")) multiplexer_1 (
    .in0(subtractor_1_out), .in1(4'b0000), .out(multiplexer_1_out), .sel(and_2_out));
  Multiplexer #(.width(4), .enable("false")) multiplexer_2 (
    .in0(multiplexer_1_out), .in1(4'b1111), .out(Exponent_Output), .sel(and_1_out));
  xor xor_1 (xor_1_out, Significand[15], 1'b1);
  nor nor_1 (nor_1_out, subtractor_1_out[0], subtractor_1_out[1], subtractor_1_out[2], subtractor_1_out[3]);
  or or_1 (or_1_out, subtractor_1_bout, nor_1_out);
  Set_Bit_Finder set_bit_finder_1 (
    .Input(Significand), .Shift_Amount(set_bit_finder_1_shift_amount), .One_Present(Not_All_Zero));
  Subtractor #(.width(4)) subtractor_2 (
    .a(Exponent), .b(4'b0000), .out(subtractor_2_out), .bin(nor_1_out));  // open: bout
  and and_2 (and_2_out, xor_1_out, or_1_out);
  and and_3 (and_3_out, Exponent_Output[0], Exponent_Output[1], Exponent_Output[2], Exponent_Output[3]);
  Multiplexer #(.width(4), .enable("false")) multiplexer_3 (
    .in0(set_bit_finder_1_shift_amount), .in1(subtractor_2_out), .out(multiplexer_3_out), .sel(and_2_out));
  Shifter #(.width(16), .shift("rl")) shifter_1 (.in(Significand), .\dist (multiplexer_3_out), .out(shifter_1_out));
  Multiplexer #(.width(16), .enable("false")) multiplexer_4 (
    .in0({1'b0, shifter_1_out[14:0]}), .in1(16'h4000), .out(Significand_Output), .sel(and_3_out));
endmodule

// Set Bit \nFinder
module Set_Bit_Finder (
  input  [15:0] Input,
  output [3:0] Shift_Amount,
  output One_Present
);

  wire [3:0] bitfinder_1_index;

  BitFinder #(.width(16)) bitfinder_1 (
    .in({Input[0], Input[1], Input[2], Input[3], Input[4], Input[5], Input[6], Input[7], Input[8], Input[9], Input[10], Input[11], Input[12], Input[13], Input[14], Input[15]}),
    .index(bitfinder_1_index), .found(One_Present));
  Subtractor #(.width(4)) subtractor_1 (
    .a(bitfinder_1_index), .b(4'b0000), .out(Shift_Amount), .bin(1'b1));  // open: bout
endmodule

module Compare (
  input  [3:0] Exponent_A,
  input  [3:0] Exponent_B,
  output [3:0] Exponent_Difference,
  output Exponent_A___Exponent_B
);

  wire [3:0] negator_1_out, subtractor_1_out;

  Subtractor #(.width(4)) subtractor_1 (
    .a(Exponent_B), .b(Exponent_A), .out(subtractor_1_out), .bin(1'b0), .bout(Exponent_A___Exponent_B));
  Negator #(.width(4)) negator_1 (.in(subtractor_1_out), .out(negator_1_out));
  Multiplexer #(.width(4), .disabled(0), .enable("false")) multiplexer_1 (
    .in0(subtractor_1_out), .in1(negator_1_out), .out(Exponent_Difference), .sel(Exponent_A___Exponent_B));
endmodule

module Padder (
  input  [3:0] Exponent,
  input  [10:0] Fraction,
  output [15:0] Significand
);

  or or_1 (Significand[14], Exponent[0], Exponent[1], Exponent[2], Exponent[3]);

  assign {Significand[15], Significand[13:0]} = {1'b0, Fraction, 3'b000};
endmodule

module Adder (
  input  [15:0] Significand_1,
  input  [15:0] Signifiand_2,
  input  Sign1,
  input  Sign2,
  output [15:0] Output_Significand,
  output Sign_Output
);

  wire comparator_1_lt, xor_1_out;
  wire [15:0] multiplexer_1_out, multiplexer_2_out, multiplexer_3_out, negator_1_out;

  Comparator #(.width(16)) comparator_1 (.a(Significand_1), .b(Signifiand_2), .lt(comparator_1_lt));  // open: gt, eq
  Multiplexer #(.width(16), .enable("false")) multiplexer_1 (
    .in0(Signifiand_2), .in1(Significand_1), .out(multiplexer_1_out), .sel(comparator_1_lt));
  Multiplexer #(.width(16), .enable("false")) multiplexer_2 (
    .in0(Significand_1), .in1(Signifiand_2), .out(multiplexer_2_out), .sel(comparator_1_lt));
  xor xor_1 (xor_1_out, Sign1, Sign2);
  Negator #(.width(16)) negator_1 (.in(multiplexer_1_out), .out(negator_1_out));
  Multiplexer #(.width(16), .enable("false")) multiplexer_3 (
    .in0(multiplexer_1_out), .in1(negator_1_out), .out(multiplexer_3_out), .sel(xor_1_out));
  Multiplexer #(.enable("false")) multiplexer_4 (.in0(Sign1), .in1(Sign2), .out(Sign_Output), .sel(comparator_1_lt));
  Adder_part #(.width(16)) adder_1 (
    .a(multiplexer_3_out), .b(multiplexer_2_out), .out(Output_Significand));  // open: cin, cout
endmodule

// Rounding\nHardware
module Rounding_Hardware (
  input  [15:0] Significand_Input,
  input  [3:0] Exponent_Input,
  output [15:0] Significand_Output,
  output [3:0] Exponent_Output,
  output Overflow
);

  wire [15:0] adder_1_out;

  Adder_part #(.width(16)) adder_1 (
    .a(Significand_Input), .b({{12{1'b0}}, Significand_Input[2], 3'b000}), .out(adder_1_out), .cin(1'b0));  // open: cout
  Adder_part #(.width(4)) adder_2 (
    .a(Exponent_Input), .b(4'b0000), .out(Exponent_Output), .cin(adder_1_out[15]));  // open: cout
  Shifter #(.width(16), .shift("lr")) shifter_1 (
    .in(adder_1_out), .\dist ({3'b000, adder_1_out[15]}), .out(Significand_Output));
  and and_1 (Overflow, Exponent_Output[0], Exponent_Output[1], Exponent_Output[2], Exponent_Output[3]);
endmodule

module Floating_Point_Adder (
  input  [15:0] Number_A,
  input  [15:0] Number_B,
  output [15:0] Output,
  output Overflow,
  output Underflow
);

  wire compare_1_exponent_a___exponent_b, multiplexer_1_out, multiplexer_2_out,
       normalizing_hardware_1_not_all_zero, overflow_underflow_1_overflow, rounding_hardware_1_overflow;
  wire [3:0] compare_1_exponent_difference, multiplexer_3_out, normalizing_hardware_1_exponent_output;
  wire [15:0] adder_1_output_significand, multiplexer_4_out, multiplexer_5_out,
       normalizing_hardware_1_significand_output, padder_1_significand, padder_2_significand,
       rounding_hardware_1_significand_output, shifter_1_out;

  Multiplexer #(.enable("false")) multiplexer_1 (
    .in0(Number_B[15]), .in1(Number_A[15]), .out(multiplexer_1_out), .sel(compare_1_exponent_a___exponent_b));
  Multiplexer #(.enable("false")) multiplexer_2 (
    .in0(Number_A[15]), .in1(Number_B[15]), .out(multiplexer_2_out), .sel(compare_1_exponent_a___exponent_b));
  Padder padder_1 (.Exponent(Number_A[14:11]), .Fraction(Number_A[10:0]), .Significand(padder_1_significand));
  Multiplexer #(.width(4), .disabled(0), .enable("false")) multiplexer_3 (
    .in0(Number_B[14:11]), .in1(Number_A[14:11]), .out(multiplexer_3_out),
    .sel(compare_1_exponent_a___exponent_b));
  Rounding_Hardware rounding_hardware_1 (
    .Significand_Input(normalizing_hardware_1_significand_output),
    .Significand_Output({rounding_hardware_1_significand_output[15:14], Output[10:0], rounding_hardware_1_significand_output[2:0]}),
    .Exponent_Output(Output[14:11]), .Exponent_Input(normalizing_hardware_1_exponent_output),
    .Overflow(rounding_hardware_1_overflow));
  Compare compare_1 (
    .Exponent_Difference(compare_1_exponent_difference),
    .Exponent_A___Exponent_B(compare_1_exponent_a___exponent_b), .Exponent_A(Number_A[14:11]),
    .Exponent_B(Number_B[14:11]));
  Adder adder_1 (
    .Significand_1(multiplexer_4_out), .Signifiand_2(shifter_1_out),
    .Output_Significand(adder_1_output_significand), .Sign1(multiplexer_1_out), .Sign2(multiplexer_2_out),
    .Sign_Output(Output[15]));
  Normalizing_Hardware normalizing_hardware_1 (
    .Significand(adder_1_output_significand), .Significand_Output(normalizing_hardware_1_significand_output),
    .Exponent(multiplexer_3_out), .Exponent_Output(normalizing_hardware_1_exponent_output),
    .Not_All_Zero(normalizing_hardware_1_not_all_zero));
  or or_1 (Overflow, rounding_hardware_1_overflow, overflow_underflow_1_overflow);
  Overflow_Underflow overflow_underflow_1 (
    .Exponent(normalizing_hardware_1_exponent_output), .Overflow(overflow_underflow_1_overflow),
    .Not_All_Zero(normalizing_hardware_1_not_all_zero), .Underflow(Underflow));
  Padder padder_2 (.Exponent(Number_B[14:11]), .Fraction(Number_B[10:0]), .Significand(padder_2_significand));
  Multiplexer #(.width(16), .disabled(0), .enable("false")) multiplexer_4 (
    .in0(padder_2_significand), .in1(padder_1_significand), .out(multiplexer_4_out),
    .sel(compare_1_exponent_a___exponent_b));
  Shifter #(.width(16), .shift("lr")) shifter_1 (
    .in(multiplexer_5_out), .\dist (compare_1_exponent_difference), .out(shifter_1_out));
  Multiplexer #(.width(16), .enable("false")) multiplexer_5 (
    .in0(padder_1_significand), .in1(padder_2_significand), .out(multiplexer_5_out),
    .sel(compare_1_exponent_a___exponent_b));
endmodule

module Block_Diagram (
  input  [15:0] Number_A,
  input  [15:0] Number_B,
  output Overflow,
  output Underflow,
  output [15:0] out_5
);

  Floating_Point_Adder floating_point_adder_1 (
    .Number_A(Number_A), .Number_B(Number_B), .Underflow(Underflow), .Overflow(Overflow), .Output(out_5));
endmodule

// Overflow\nUnderflow
module Overflow_Underflow (
  input  [3:0] Exponent,
  input  Not_All_Zero,
  output Overflow,
  output Underflow
);

  wire nor_1_out;

  and and_1 (Overflow, Exponent[0], Exponent[1], Exponent[2], Exponent[3]);
  nor nor_1 (nor_1_out, Exponent[0], Exponent[1], Exponent[2], Exponent[3]);
  and and_2 (Underflow, nor_1_out, Not_All_Zero);
endmodule
